# Fritzing sketch PiLN (saved by Fritzing 0.9.3b)
circuit board: 10cm x 6cm
perfboards: 1

parts:
  Raspberry_Pi_1 = Raspberry Pi 3 [part_number=RPI-3-V1.2]
  Part1 = Adafruit Thermocouple Amplifier MAX31855 [part_number="Adafruit #269"]
  LCD1 = LCD screen
  R1 = Trimmer Potentiometer [maximum_resistance=10kΩ package=THT]
  U1 = RELAY-SOLIDSTATE [package=relay-s108t02]
  U3 = RELAY-SOLIDSTATE [package=relay-s108t02]
  LED1 = smd LED [color="Red (633nm)" package="0805 [SMD]"]
  R2 = Resistor [tolerance=±5% resistance=220 package=THT]
  U4 = RELAY-SOLIDSTATE [package=relay-s108t02]

nets:
  3V3: Raspberry_Pi_1.3v3, Raspberry_Pi_1.3V3, Part1.VIN
  N1: Raspberry_Pi_1.GIPO4, U1.+
  GND: Raspberry_Pi_1.GND, Part1.GND, R1.leg1, U1.-, U3.-, LED1.cathode, U4.-
  N2: Raspberry_Pi_1.GIPO17, LCD1.RS
  N3: Raspberry_Pi_1.GIPO27, LCD1.E
  N4: Raspberry_Pi_1.GIPO21, LCD1.DB7
  N5: Raspberry_Pi_1.GIPO20, LCD1.DB6
  N6: Raspberry_Pi_1.GIPO16, LCD1.DB5
  N7: Raspberry_Pi_1.GIPO12, LCD1.DB4
  N8: Raspberry_Pi_1.GIPO25, Part1.CLK
  N9: Raspberry_Pi_1.GIPO24, Part1.CS
  N10: Raspberry_Pi_1.GIPO18, Part1.DO
  5V: Raspberry_Pi_1.5V, LCD1.VDD, LCD1.LED+, R1.leg2, U1.T2
  N11: LCD1.VSS, LCD1.R/W, LCD1.LED-
  N12: LCD1.V0, R1.wiper
  N13: U1.T1, U3.+, R2.Pin_1, U4.+
  N14: LED1.anode, R2.Pin_0

notes:
  Relay on indicator LED
  Relay Pair x 3 for 3 heating coils
  220 VAC In
  To heating coils

custom parts:
  Adafruit Thermocouple Amplifier MAX31855: Thermocouples are very sensitive, requiring a good amplifier with a cold-compensation reference. The MAX31855K does everything for you, and can be easily interfaced with any microcontroller, even one without an analog input. This breakout board has the chip itself, a 3.3V regulator with 10uF bypass capacitors and level shifting circuitry, all assembled and tested. Comes with a 2 pin terminal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
